# Fritzing sketch jarmilka (saved by Fritzing 0.9.2b)
breadboards: 1

parts:
  Raspberry_Pi_B_rev2 = Raspberry Pi B rev2
  R1 = Resistor [tolerance=±5% resistance=1k package=THT]
  R2 = Resistor [tolerance=±5% resistance=1k package=THT]
  R3 = Resistor [tolerance=±5% resistance=1k package=THT]
  LED1 = LED - 3mm [color="Green (570nm)" package="3 mm [THT]"]
  LED2 = LED - 3mm [color="Green (570nm)" package="3 mm [THT]"]
  LED3 = LED - 3mm [color="Green (570nm)" package="3 mm [THT]"]
  S1 = Pushbutton [package="[THT]"]

nets:
  N1: Raspberry_Pi_B_rev2.GPIO_2, R1.Pin_0
  N2: Raspberry_Pi_B_rev2.GPIO_3, R2.Pin_0
  N3: Raspberry_Pi_B_rev2.GND, LED1.cathode, LED2.cathode, LED3.cathode, S1.Pin_1, S1.Pin_2
  N4: Raspberry_Pi_B_rev2.GPIO_15, S1.Pin_3, S1.Pin_4
  N5: Raspberry_Pi_B_rev2.GPIO_4, R3.Pin_0
  N6: R1.Pin_1, LED1.anode
  N7: R2.Pin_1, LED2.anode
  N8: R3.Pin_1, LED3.anode
